# Fritzing sketch RainGauge (saved by Fritzing 0.9.3b)
breadboards: 1

parts:
  VCC1 = 4 x AAA Battery Mount
  LED1 = smd LED [color="Green (555nm)" package="0805 [SMD]"]
  U2 = mystery part, 3 pins [chip_label=AH180]
  U3 = NodeMCU V1.0
  S4 = Round Pushbutton

nets:
  N1: VCC1.-, LED1.anode, U2.pin2, U3.GND
  N2: VCC1.+, U3.Vin
  N3: LED1.cathode, U3.D2
  N4: U2.pin1, U3.3V3, S4.leg1
  N5: U2.pin3, U3.D1
  N6: U3.D4, S4.leg0

custom parts:
  NodeMCU V1.0: ESP8266 based NodeMCU
